# Fritzing sketch schema (saved by Fritzing 1.0.4)

parts:
  Présence_Devant_Portail = HC-SR04 Ultrasonic Distance Sensor
  Infos_Portail_Fermé = Camdenboss CTB0158-2 [part_number=CTB0158-2 package=THT]
  Ouverture_portail = 1 chan 3v relay module
  Commande_Portail = Camdenboss CTB0158-4 [part_number=CTB0158-4 package=THT]
  Arduino_BLE_/_WIFI = Arduino Nano ESP32
  Présence_Devant_Portillon = HC-SR04 Ultrasonic Distance Sensor

nets:
  5v: Présence_Devant_Portail.VCC, Arduino_BLE_/_WIFI.Pin_12, Présence_Devant_Portillon.VCC
  N1: Présence_Devant_Portail.TRIG, Arduino_BLE_/_WIFI.Pin_26
  N2: Présence_Devant_Portail.ECHO, Arduino_BLE_/_WIFI.Pin_25
  GND: Présence_Devant_Portail.GND, Infos_Portail_Fermé.pin2, Ouverture_portail.pin_3, Arduino_BLE_/_WIFI.Pin_14, Arduino_BLE_/_WIFI.Pin_19, Présence_Devant_Portillon.GND
  N3: Infos_Portail_Fermé.pin1, Arduino_BLE_/_WIFI.Pin_20
  3.3v: Ouverture_portail.pin_1, Arduino_BLE_/_WIFI.Pin_2
  N4: Ouverture_portail.pin_2, Arduino_BLE_/_WIFI.Pin_22
  N5: Ouverture_portail.pin_4, Ouverture_portail.pin_5
  N6: Ouverture_portail.pin_6, Commande_Portail.pin3
  N7: Ouverture_portail.pin_7, Commande_Portail.pin2
  N8: Ouverture_portail.pin_9, Ouverture_portail.pin_10
  5V: Arduino_BLE_/_WIFI.Pin_15
  N9: Arduino_BLE_/_WIFI.Pin_27, Présence_Devant_Portillon.ECHO
  N10: Arduino_BLE_/_WIFI.Pin_28, Présence_Devant_Portillon.TRIG

notes:
  Alimentation par USB

custom parts:
  1 chan 3v relay module: Single 3V relay isolated drive control module High level drive board.
  Arduino Nano ESP32: Arduino® Nano ESP32 smd.
